# Fritzing sketch jack-o-lantern (saved by Fritzing 0.9.3b)

parts:
  SPKR1 = Loudspeaker  # not connected
  U1 = Packages: [package=dil28-3]
  Raspberry_Pi2 = Raspberry Pi B rev2
  LED1 = LED - 5mm [color="Red (633nm)" package="5 mm [THT]"]
  LED2 = LED - 5mm [color="Red (633nm)" package="5 mm [THT]"]
  PIR1 = PIR sensor

nets:
  N1: U1.OUT7, LED2.cathode
  N2: U1.GSCLK, Raspberry_Pi2.GPIO_18
  VCC: U1.VCC, Raspberry_Pi2.5V, LED1.anode, LED2.anode, PIR1.VDD
  GND: U1.GND, Raspberry_Pi2.GND, PIR1.GND
  N3: U1.BLANK, Raspberry_Pi2.GPIO_27
  N4: U1.XLAT, Raspberry_Pi2.GPIO_17
  N5: U1.SCLK, Raspberry_Pi2.GPIO_24
  N6: U1.SIN, Raspberry_Pi2.GPIO_23
  N7: U1.VPRG, Raspberry_Pi2.GPIO_22
  N8: U1.OUT0, LED1.cathode
  N9: Raspberry_Pi2.GPIO_4, PIR1.SIG
